# Fritzing sketch Untitled Sketch (saved by Fritzing 0.9.3b)

parts:
  U1 = LuaNode32 / ESP32 [part_number=ESP32S-PIN30]
  U2 = Texas Instruments DRV8833
  M1 = DC Motor
  M2 = DC Motor
  VCC1 = Battery block 9V

nets:
  N1: U1.D27, U2.IN1
  N2: U1.D14, U2.IN2
  N3: U1.D12, U2.IN3
  N4: U1.D13, U2.IN4
  GND: U1.GND, U2.GND
  VIN: U1.Vin, U2.VCC, VCC1.+
  N5: U2.OUT1, M2.pin_1
  N6: U2.OUT2, M2.pin_2
  N7: U2.OUT3, M1.pin_1
  N8: U2.OUT4, M1.pin_2

custom parts:
  LuaNode32 / ESP32: New Image for LuaNode32 DOIT ESP32 DEVKIT V1. Base parts from LuaNode32 / ESP32 ESP32 based LuaNode32 by G.Noorlander DOIT Esp32 DevKit v1 (30 pins long, 11 pins width) by Werner Rothschopf (modified by vanepp Dec 2018)
  Texas Instruments DRV8833: The DRV8833 provides a dual bridge motor driver solution for toys, printers, and other mechatronic applications.
